# Fritzing sketch led1 (saved by Fritzing 0.9.3b)
breadboards: 1

parts:
  Part1 = Arduino Uno (Rev3)
  R1 = Resistor [tolerance=±5% resistance=220 package=THT]
  LED1 = LED - 5mm [color="Green (565nm)" package="5 mm [THT]"]
  LED2 = LED - 5mm [color="Red (633nm)" package="5 mm [THT]"]
  R2 = Resistor [tolerance=±5% resistance=220 package=THT]

nets:
  N1: Part1.D8, R1.Pin_0
  N2: Part1.D13/SCK, R2.Pin_1
  N3: Part1.GND, LED1.cathode, LED2.cathode
  N4: R1.Pin_1, LED1.anode
  N5: LED2.anode, R2.Pin_0

notes:
  V I R P
  LED1 2.69 9.7mA 277Ohm 18.00mW
  R1 2.32 9.7mA 249Ohm 15.5mW
  T1 5.01 9.7mA 526Ohm 33.5mW
  LED2 1.76 8.3mA 212Ohm 14.6mW
  R1 2.32 8.3mA 276Ohm 19.3mW
  T1 5.01 8.3mA 488Ohm 33.9mW
  Michael Cleverdon
  Anode Cathode
