# Fritzing sketch lm358 (saved by Fritzing 0.9.3b)
breadboards: 1

parts:
  Part1 = Arduino Mega 2560 (Rev3)
  R1 = Resistor [tolerance=±5% resistance=1k package=THT]
  R2 = Photocell (LDR) [package=THT]
  U1 = LM 358 Dual Op-Amp [package="DIP8 [THT]"]
  R3 = Resistor [tolerance=±5% resistance=1k package=THT]
  R4 = Resistor [tolerance=±5% resistance=1k package=THT]
  Q1 = NPN-Transistor [package="TO92 [THT]"]
  LED1 = LED - 5mm [color="Red (633nm)" package="5 mm [THT]"]

nets:
  N1: Part1.3V3, U1.connector7
  N2: Part1.5V, R1.Pin_0
  N3: Part1.GND, R2.pin_1, U1.connector3, R4.Pin_1, Q1.E
  N4: Part1.D7_PWM, Q1.B
  N5: R1.Pin_1, R2.pin_0, U1.connector2
  N6: U1.connector0, R3.Pin_0, LED1.anode
  N7: U1.connector1, R3.Pin_1, R4.Pin_0
  N8: Q1.C, LED1.cathode
