# Fritzing sketch sketch? (saved by Fritzing 0.9.3b)
breadboards: 1

parts:
  R1 = Photocell (LDR) [package=THT]
  R2 = Resistor [tolerance=±5% resistance=220 package=THT]
  LED1 = RGB LED - (4 legs) [package="5 mm [THT]"]
  R3 = Resistor [tolerance=±5% resistance=220 package=THT]
  R4 = Resistor [tolerance=±5% resistance=220 package=THT]
  R5 = Resistor [tolerance=±5% resistance=220 package=THT]
  Part1 = Arduino Mega ADK (Rev3)

nets:
  N1: R1.pin_0, R2.Pin_1, Part1.A0
  N2: R1.pin_1, LED1.common_anode, Part1.5V
  N3: R2.Pin_0, Part1.GND
  N4: LED1.red_cathode, R3.Pin_0
  N5: LED1.green_cathode, R4.Pin_1
  N6: LED1.blue_cathode, R5.Pin_1
  N7: R3.Pin_1, Part1.D11_PWM
  N8: R4.Pin_0, Part1.D10_PWM
  N9: R5.Pin_0, Part1.D9_PWM

notes:
  MichaelC
