# Fritzing sketch total (saved by Fritzing 0.9.3b)
breadboards: 1

parts:
  Part1 = Arduino Mega 2560 (Rev3)
  R2 = Photocell (LDR) [package=THT]
  R3 = Resistor [tolerance=±5% resistance=1k package=THT]
  LED2 = RGB LED - (4 legs) [package="5 mm [THT]"]
  R4 = Resistor [tolerance=±5% resistance=220 package=THT]
  R5 = Resistor [tolerance=±5% resistance=220 package=THT]
  R6 = Resistor [tolerance=±5% resistance=220 package=THT]
  J1 = Piezo Speaker
  R7 = Resistor [tolerance=±5% resistance=220 package=THT]
  R8 = Resistor [tolerance=±5% resistance=220 package=THT]
  R9 = Resistor [tolerance=±5% resistance=220 package=THT]
  R10 = Resistor [tolerance=±5% resistance=220 package=THT]
  R11 = Resistor [tolerance=±5% resistance=220 package=THT]
  LED1 = LED - 3mm [color="Red (633nm)" package="3 mm [THT]"]
  LED3 = LED - 3mm [color="Yellow (592nm)" package="3 mm [THT]"]
  LED4 = LED - 3mm [color="Green (560nm)" package="3 mm [THT]"]
  LED5 = LED - 3mm [color="Blue (430nm)" package="3 mm [THT]"]
  LED6 = LED - 3mm [color="White (6500K)" package="3 mm [THT]"]

nets:
  N1: Part1.A0, R2.pin_1, R3.Pin_0
  N2: Part1.D13_PWM, R4.Pin_1
  N3: Part1.D12_PWM, R5.Pin_0
  N4: Part1.D11_PWM, R6.Pin_0
  N5: Part1.D10_PWM, LED1.anode
  N6: Part1.D9_PWM, LED3.anode
  N7: Part1.D8_PWM, LED4.anode
  N8: Part1.5V, LED2.common_anode, J1.pin1
  N9: Part1.GND, R3.Pin_1, R7.Pin_0, R8.Pin_0, R9.Pin_0, R10.Pin_0, R11.Pin_0
  N10: Part1.D3_PWM, J1.pin2
  N11: Part1.D6_PWM, LED6.anode
  N12: Part1.D7_PWM, LED5.anode
  N13: LED2.red_cathode, R4.Pin_0
  N14: LED2.green_cathode, R5.Pin_1
  N15: LED2.blue_cathode, R6.Pin_1
  N16: R7.Pin_1, LED1.cathode
  N17: R8.Pin_1, LED3.cathode
  N18: R9.Pin_1, LED4.cathode
  N19: R10.Pin_1, LED5.cathode
  N20: R11.Pin_1, LED6.cathode
